# Fritzing sketch sketch (saved by Fritzing 0.9.4)
breadboards: 1

parts:
  Raspberry_Pi1 = Raspberry Pi B+
  LED1 = smd LED [color="Green (555nm)" package="0603 [SMD]"]
  R1 = Resistor [tolerance=±5% resistance=470 package="1206 [SMD]"]
  R2 = Resistor [tolerance=±5% resistance=470 package="1206 [SMD]"]
  LED2 = smd LED [color="Red (633nm)" package="0603 [SMD]"]
  U1 = TCM8240MD [package=tcm8240md]  # not connected

nets:
  N1: Raspberry_Pi1.GND, LED1.cathode, LED1.anode, R1.Pin_0, R2.Pin_0, LED2.cathode, LED2.anode
  N2: Raspberry_Pi1.GPIO17, R1.Pin_1
  N3: Raspberry_Pi1.GPIO27, R2.Pin_1
