# Fritzing sketch sketch (saved by Fritzing 0.9.4)
breadboards: 1

parts:
  Raspberry_Pi2 = Raspberry Pi B+
  LED4 = smd LED [color="Green (555nm)" package="0603 [SMD]"]
  R4 = Resistor [tolerance=±5% resistance=470 package="1206 [SMD]"]

nets:
  N1: Raspberry_Pi2.GND, LED4.cathode, LED4.anode, R4.Pin_0
  N2: Raspberry_Pi2.GPIO17, R4.Pin_1
